# Fritzing sketch Semaforo (saved by Fritzing 0.9.3b)
breadboards: 1

parts:
  LED1 = LED - 5mm [color="Red (633nm)" package="5 mm [THT]"]
  LED3 = LED - 5mm [color="Green (555nm)" package="5 mm [THT]"]
  LED2 = LED - 5mm [color="Yellow (585nm)" package="5 mm [THT]"]
  Componente1 = Arduino Uno (Rev3) - ICSP

nets:
  N1: LED1.cathode, LED3.cathode, LED2.cathode, Componente1.GND
  N2: LED1.anode, Componente1.D10_PWM/SS
  N3: LED3.anode, Componente1.D12/MISO
  N4: LED2.anode, Componente1.ICSP_MOSI, Componente1.D11_PWM/MOSI

// code stored in the sketch: SEMAFORO.ino
int LED_ROJO=A0;//se nombran los pines con su respectivo color
int LED_AMARILLO=A1;
int LED_VERDE=A2;
int i=0;//variable para el contador del led verde para intermitencia

void setup (){
  pinMode(LED_ROJO, OUTPUT);//se definen los led como pines de salida
  pinMode(LED_AMARILLO, OUTPUT);
  pinMode(LED_VERDE, OUTPUT);
 }
  
void loop(){
analogWrite(LED_ROJO,0);//se inicia con todos los led apagados para no alargar el codigo
analogWrite(LED_AMARILLO,0);
analogWrite(LED_VERDE,0);
delay(10);

analogWrite(LED_VERDE,676);//se utiliza 676 bits puesto que es el aproximado a 3.3 V en la conversión, donde 1023bits son 5V
delay(8000);//se enciende el led verde por 8 segundos

i=0;
while (i<5){
  analogWrite(LED_VERDE,0);//el led verde titila 4 veces con un tiempo de 0.3 segundos encendido y 0.3 apagado
  delay(300);
  analogWrite(LED_VERDE,676);
  delay(300);
  i=i+1;  
  }

analogWrite(LED_VERDE,0);//se apaga el led verde
analogWrite(LED_AMARILLO,676);//se enciende el led amarillo por 2.5 segundos
delay(2500);

analogWrite(LED_AMARILLO,0);//se apaga el led amarillo
analogWrite(LED_ROJO,676);//se enciende el led rojo por 7 segundos
delay(7000); 
}
